// Logisim project FlipFlop SR.circ as structural Verilog: 1 circuit, main circuit main
module main (
  input  RESET,
  input  SET,
  output Q
);

  wire and_1_out, and_2_out, CLOCK_out, nor_2_out;

  Clock CLOCK (.out(CLOCK_out));
  and and_1 (and_1_out, RESET, CLOCK_out);
  and and_2 (and_2_out, CLOCK_out, SET);
  nor nor_1 (Q, and_1_out, nor_2_out);
  nor nor_2 (nor_2_out, Q, and_2_out);
endmodule
