// Logisim project FullAdder_2bit.circ as structural Verilog: 1 circuit, main circuit main
module main (
  input  A,
  input  B,
  input  Ci,
  output S,
  output Co
);

  wire and_1_out, and_2_out, xor_2_out;

  _7_Segment_Display u_7_segment_display_1 (.b(S), .c(S));  // open: g, f, a, e, d, dp
  xor xor_1 (S, xor_2_out, Ci);
  or or_1 (Co, and_1_out, and_2_out);
  and and_1 (and_1_out, xor_2_out, Ci);
  and and_2 (and_2_out, A, B);
  xor xor_2 (xor_2_out, A, B);

  // Notes on the sheet:
  //   11+
  //   01=
  //   100
endmodule
