// Logisim project FullAdder_InCascata.circ as structural Verilog: 1 circuit, main circuit main
module main (
  input  A2,
  input  A1,
  input  B2,
  input  B1,
  input  Ci,
  output S2,
  output S1,
  output Co
);

  wire and_1_out, and_2_out, and_3_out, and_4_out, and_5_out, not_1_out, or_2_out, or_3_out, xor_2_out,
       xor_4_out;

  _7_Segment_Display u_7_segment_display_1 (.b(Co), .c(Co));  // open: g, f, a, e, d, dp
  _7_Segment_Display u_7_segment_display_2 (.b(S2), .c(S2));  // open: g, f, a, e, d, dp
  xor xor_1 (S2, xor_2_out, or_3_out);
  or or_1 (Co, and_1_out, and_2_out);
  and and_1 (and_1_out, xor_2_out, or_3_out);
  and and_2 (and_2_out, A2, B2);
  and and_3 (and_3_out, S2, S1);
  xor xor_2 (xor_2_out, A2, B2);
  not not_1 (not_1_out, S1);
  _7_Segment_Display u_7_segment_display_3 (.a(or_2_out));  // open: g, f, b, e, d, c, dp
  or or_2 (or_2_out, and_3_out, not_1_out);
  _7_Segment_Display u_7_segment_display_4 (.b(S1), .c(S1));  // open: g, f, a, e, d, dp
  xor xor_3 (S1, xor_4_out, Ci);
  or or_3 (or_3_out, and_4_out, and_5_out);
  and and_4 (and_4_out, xor_4_out, Ci);
  and and_5 (and_5_out, A1, B1);
  xor xor_4 (xor_4_out, A1, B1);

  // Notes on the sheet:
  //   11+
  //   01=
  //   100
endmodule
