// Logisim project Latch D.circ as structural Verilog: 1 circuit, main circuit main
module main (
  input  SET,
  input  RESET,
  output Q
);

  wire nand_1_out, nand_2_out, nand_4_out;

  nand nand_1 (nand_1_out, SET, nand_2_out);
  nand nand_2 (nand_2_out, nand_1_out, RESET);
  nand nand_3 (Q, nand_1_out, nand_4_out);
  nand nand_4 (nand_4_out, Q, nand_2_out);
endmodule
