// Logisim project Latch SR con ENABLE.circ as structural Verilog: 1 circuit, main circuit main
module main (
  input  RESET,
  input  ENABLE,
  input  SET,
  output Q
);

  wire and_1_out, and_2_out, nor_2_out;

  and and_1 (and_1_out, RESET, ENABLE);
  and and_2 (and_2_out, ENABLE, SET);
  nor nor_1 (Q, and_1_out, nor_2_out);
  nor nor_2 (nor_2_out, Q, and_2_out);
endmodule
