// Logisim project Latch SR con NAND.circ as structural Verilog: 1 circuit, main circuit main
module main (
  input  SET,
  input  RESET,
  output Q
);

  wire nand_2_out, not_1_out, not_2_out;

  not not_1 (not_1_out, SET);
  not not_2 (not_2_out, RESET);
  nand nand_1 (Q, not_1_out, nand_2_out);
  nand nand_2 (nand_2_out, Q, not_2_out);
endmodule
