// Logisim project transistors.circ as structural Verilog: 1 circuit, main circuit main
module main (
  input  in_1,
  input  in_2,
  input  in_3,
  input  in_4,
  output out_5,
  output out_6
);

  Transistor #(.\type ("n")) transistor_1 (.in(in_2), .out(out_5), .gate(in_1));
  Transistor transistor_2 (.in(in_4), .out(out_6), .gate(in_3));

  // Notes on the sheet:
  //   NPN
  //   PNP
endmodule
